# Fritzing sketch 3D Scanner basic (saved by Fritzing 1.0.2b)

parts:
  Arduino_CNC_Shield_V3_00_1 = Arduino_CNC_V3.00
  M1 = Stepper Motor - Bipolar
  M2 = Stepper Motor - Bipolar
  S1 = Limit Switch [package="Breakout Board"]
  BT1 = Bluetooth HC-06u [package=THT]
  Mosfet_driver_module1 = IFR520 MOS module [package=THT]
  U1 = 2.5mm Audio Jack [package=stereojack2.5mm_stereojack2.5mm]

nets (from the breadboard view):
  N1: Arduino_CNC_Shield_V3_00_1.GND#12, Mosfet_driver_module1.pin3
  N2: Arduino_CNC_Shield_V3_00_1.X-MTR_'1', M2.A
  N3: Arduino_CNC_Shield_V3_00_1.X-MTR_'2', M2.C
  N4: Arduino_CNC_Shield_V3_00_1.X-MTR_'3', M2.B
  N5: Arduino_CNC_Shield_V3_00_1.X-MTR_'4', M2.D
  N6: Arduino_CNC_Shield_V3_00_1.Y-MTR_'1', M1.A
  N7: Arduino_CNC_Shield_V3_00_1.Y-MTR_'2', M1.C
  N8: Arduino_CNC_Shield_V3_00_1.Y-MTR_'3', M1.B
  N9: Arduino_CNC_Shield_V3_00_1.Y-MTR_'4', M1.D
  N10: Arduino_CNC_Shield_V3_00_1.RX, BT1.RXD
  N11: Arduino_CNC_Shield_V3_00_1.TX, BT1.TXD
  5V: Arduino_CNC_Shield_V3_00_1.5V, BT1.VCC
  N12: Arduino_CNC_Shield_V3_00_1.GND#76, BT1.GND
  N13: Arduino_CNC_Shield_V3_00_1.End_Stops_Y+_(Gnd), S1.S
  N14: Arduino_CNC_Shield_V3_00_1.End_Stops_Y-_(Gnd), S1.V
  N15: Arduino_CNC_Shield_V3_00_1.SpnEn_(Gnd), Mosfet_driver_module1.pin1
  N16: Mosfet_driver_module1.pin5, U1.RIGHT
  N17: Mosfet_driver_module1.pin7, U1.SLEEVE

custom parts:
  Arduino_CNC_V3.00: Protoneer Arduino CNC Shield V3.00 If using Grbl V0.9: The “A” axis can not be used (yet). The “SCL” (Arduino A5) pin is now used for 'Probing' input. The “End Stops Z+ & Z-” (Arduino D11) and “SpnEn” (Arduino D12) have been switched!
  Limit Switch: Generic limit switch commonly found on 3D printers. Typical lever microswitch mounted on a PCB board with a 3 pin JST XH connector.
  Bluetooth HC-06u: Bluetooth HC-06 - face up, pins down 16.5mm x 37.5mm PCB
  IFR520 MOS module: Breakout board for the IFR520 MOSFET transistor. The module is designed to switch heavy DC loads from a single digital pin of your microcontroller. Its main purpose is to provide a low cost way to drive a DC motor for robotics applications, but the module can be used to control most high current DC loads. Screw terminals are provided to interface to your load and external power source. An LED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
